# Fritzing sketch 实验1.1 (saved by Fritzing 0.9.3b)
breadboards: 1

parts:
  IC1 = IC, DIP package, 14 pins [chip_label=7400]
  IC3 = IC, DIP package, 14 pins [chip_label=7420]

nets:
  N1: IC1.pin1, IC1.pin10
  N2: IC1.pin2, IC1.pin14, IC3.pin2, IC3.pin14
  N3: IC1.pin3, IC3.pin1
  N4: IC1.pin4, IC3.pin6
  N5: IC1.pin5, IC1.pin8
  N6: IC1.pin7, IC3.pin7
  N7: IC1.pin9, IC1.pin11
  N8: IC1.pin12, IC3.pin5
  N9: IC1.pin13, IC3.pin4
